# Fritzing sketch LCD-version (saved by Fritzing 0.9.9b)
breadboards: 1

parts:
  Part1 = Arduino Uno (Rev3) - ICSP
  U1 = Sharp PC817 [package=THT]
  R1 = Resistor [tolerance=±5% resistance=1500 package="1206 [SMD]"]
  Power_plug1 = Power plug
  J1 = Dagu DGServo 9g header (male) [package=THT]
  LCD1 = LCD screen
  R2 = Trimmer Potentiometer [maximum_resistance=10kΩ package=THT]
  R3 = Resistor [tolerance=±5% power=0.25 resistance=220 package=THT]

nets:
  5V: Part1.5V, LCD1.VDD, R2.leg2, R3.Pin_0
  N1: Part1.D11_PWM/MOSI, LCD1.E
  N2: Part1.D12/MISO, LCD1.RS
  N3: Part1.D2, LCD1.DB7
  N4: Part1.D3_PWM, LCD1.DB6
  N5: Part1.D4, LCD1.DB5
  N6: Part1.D5_PWM, LCD1.DB4
  N7: Part1.D7, U1.Pin_4
  GND: Part1.GND, U1.Pin_3, LCD1.VSS, LCD1.R/W, LCD1.LED-, R2.leg1
  N8: U1.Pin_1, R1.Pin_0
  GND_2: U1.Pin_2, Power_plug1.GND, J1.gnd
  N9: R1.Pin_1, J1.pulse
  VCC: Power_plug1.VCC, J1.Vcc
  N10: LCD1.V0, R2.wiper
  N11: LCD1.LED+, R3.Pin_1

notes:
  E3Z NPN Sensor
  12V power source
