# Fritzing sketch LCD_version_finish (saved by Fritzing 0.9.6b)
breadboards: 1

parts:
  Part1 = Arduino Uno (Rev3) - ICSP
  U1 = Sharp PC817 [package=THT]
  R1 = Resistor [tolerance=±5% resistance=1500 package="1206 [SMD]"]
  Power_plug1 = Power plug
  J1 = Dagu DGServo 9g header (male) [package=THT]
  LCD1 = LCD screen
  R2 = Trimmer Potentiometer [maximum_resistance=10kΩ package=THT]
  R3 = Resistor [tolerance=±5% power=0.25 resistance=220 package=THT]
  HC-1 = HC-12 Module

nets:
  N1: Part1.ICSP_MOSI, Part1.D11_PWM/MOSI, LCD1.E
  N2: Part1.D8, HC-1.RXD
  N3: Part1.D9_PWM, HC-1.TXD
  N4: Part1.D12/MISO, LCD1.RS
  N5: Part1.D2, U1.Pin_4
  N6: Part1.D4, LCD1.DB4
  N7: Part1.D5_PWM, LCD1.DB5
  N8: Part1.D6_PWM, LCD1.DB6
  N9: Part1.D7, LCD1.DB7
  5V: Part1.5V, LCD1.VDD, R2.leg1, R3.Pin_0, HC-1.VCC
  GND: Part1.GND, U1.Pin_3, LCD1.VSS, LCD1.R/W, LCD1.LED-, R2.leg2, HC-1.GND
  N10: U1.Pin_1, R1.Pin_0
  GND_2: U1.Pin_2, Power_plug1.GND, J1.gnd
  N11: R1.Pin_1, J1.pulse
  VCC: Power_plug1.VCC, J1.Vcc
  N12: LCD1.V0, R2.wiper
  N13: LCD1.LED+, R3.Pin_1

notes:
  E3Z NPN Sensor
  12V power source
  1,5K ohm

custom parts:
  HC-12 Module: HC-12 433Mhz Module
