# Fritzing sketch finish (saved by Fritzing 0.9.10b)
breadboards: 1

parts:
  Part1 = Arduino Uno (Rev3) - ICSP
  U1 = Sharp PC817 [package=THT]
  R1 = Resistor [tolerance=±5% resistance=1500 package="1206 [SMD]"]
  Power_plug1 = Power plug
  J1 = Dagu DGServo 9g header (male) [package=THT]
  HC-1 = HC-12 Module
  BAT1 = BC9VPC [package=bc9vpc]

nets:
  N1: Part1.D8, HC-1.RXD
  N2: Part1.D9_PWM, HC-1.TXD
  N3: Part1.D2, U1.Pin_4
  5V: Part1.5V, HC-1.VCC
  GND: Part1.GND, U1.Pin_3, HC-1.GND, BAT1.V-
  N4: Part1.VIN, BAT1.V+
  N5: U1.Pin_1, R1.Pin_0
  GND_2: U1.Pin_2, Power_plug1.GND, J1.gnd
  N6: R1.Pin_1, J1.pulse
  VCC: Power_plug1.VCC, J1.Vcc

notes:
  E3Z NPN Sensor
  12V battery
  1,5K ohm

custom parts:
  HC-12 Module: HC-12 433Mhz Module
