# Fritzing sketch finish_with_LCD (saved by Fritzing 0.9.10b)
breadboards: 1

parts:
  Arduino_Uno_R3 = Arduino Uno (Rev3) - ICSP
  U1 = Sharp PC817 [package=THT]
  R1 = Resistor [tolerance=±5% resistance=1500 package="1206 [SMD]"]
  Battery_12v = Power plug
  E3Z_NPN_Sensor = Dagu DGServo 9g header (male) [package=THT]
  HC-12 = HC-12 Module
  LCD_Display = LCD screen
  LCM1602_IIC = LCM1602 IIC [part_number="LCM1602 IIC" chip_label="LCM1602 IIC" package="DIP (Dual Inline) [THT]"]
  BAT1 = BC9VPC [package=bc9vpc]

nets:
  N1: Arduino_Uno_R3.A4/SDA, LCM1602_IIC.SDA
  N2: Arduino_Uno_R3.A5/SCL, LCM1602_IIC.SCL
  VCC: Arduino_Uno_R3.5V, HC-12.VCC, LCM1602_IIC.VCC
  N3: Arduino_Uno_R3.D8, HC-12.RXD
  N4: Arduino_Uno_R3.D9_PWM, HC-12.TXD
  N5: Arduino_Uno_R3.D2, U1.Pin_4
  GND: Arduino_Uno_R3.GND, U1.Pin_3, HC-12.GND, LCM1602_IIC.GND, BAT1.V-
  N6: Arduino_Uno_R3.VIN, BAT1.V+
  N7: U1.Pin_1, R1.Pin_0
  GND_2: U1.Pin_2, Battery_12v.GND, E3Z_NPN_Sensor.gnd
  N8: R1.Pin_1, E3Z_NPN_Sensor.pulse
  VCC_2: Battery_12v.VCC, E3Z_NPN_Sensor.Vcc
  VSS: LCD_Display.VSS, LCM1602_IIC.VSS
  VDD: LCD_Display.VDD, LCM1602_IIC.VDD
  N9: LCD_Display.V0, LCM1602_IIC.V0
  N10: LCD_Display.RS, LCM1602_IIC.RS
  N11: LCD_Display.R/W, LCM1602_IIC.RW
  N12: LCD_Display.E, LCM1602_IIC.E
  N13: LCD_Display.DB0, LCM1602_IIC.D0
  N14: LCD_Display.DB1, LCM1602_IIC.D1
  N15: LCD_Display.DB2, LCM1602_IIC.D2
  N16: LCD_Display.DB3, LCM1602_IIC.D3
  N17: LCD_Display.DB4, LCM1602_IIC.D4
  N18: LCD_Display.DB5, LCM1602_IIC.D5
  N19: LCD_Display.DB6, LCM1602_IIC.D6
  N20: LCD_Display.DB7, LCM1602_IIC.D7
  N21: LCD_Display.LED+, LCM1602_IIC.A
  N22: LCD_Display.LED-, LCM1602_IIC.K
  N23: LCM1602_IIC.LED_A, LCM1602_IIC.LED_B

notes:
  E3Z NPN Sensor
  12V power source
  1,5K ohm

custom parts:
  HC-12 Module: HC-12 433Mhz Module
  LCM1602 IIC: I2C-Module to use a 1602 or 2004 LCD on with the wire.h libory Serial LCD Modul

// code stored in the sketch: finish.ino
#include <SoftwareSerial.h>
#include <LiquidCrystal_I2C.h>

// wireless communication setup
SoftwareSerial HC12(9, 8); // HC-12 TX Pin, HC-12 RX Pin

// initialize the library by associating any needed LCD interface
LiquidCrystal_I2C lcd(0x27, 16, 2);

// set up variables:
bool run_on = false; // is the run in progress?
long int start_time = 1; // start time of run
long int result_time = 0; // time of run
long int prev_time = 0; // previous time
int min_run_length = 1000; // delay time
short int photo_pin = 2; // pin to which photocell is connected
short int input_start = 1; // toggle what input is recognized as start

// functions declarations
void print_ln_lcd(String message, int col=0, int row=0, bool clear=false);
String ms_to_print(long int ms);

void setup() {
  Serial.begin(9600); // serial port to computer
  HC12.begin(9600); // serial port to HC-12
  lcd.init(); //initialize the lcd
  lcd.backlight(); //open the backlight 
  
  pinMode(photo_pin, INPUT_PULLUP);
  print_ln_lcd("Welcome!", 4, 0, true);
}

void loop(){
  if(HC12.available()){
    String message = HC12.readString();
    Serial.println(message);

    if(message=="run-started" && run_on==false){
      start_time = millis(); // save the time when the run started
      Serial.println("run-started"); // send message to serial monitor that run has started
      result_time = min_run_length; // set the result time to the minimum run length
      run_on = true; // set the run_on flag to true

      if(prev_time != 0)
      print_ln_lcd(ms_to_print(prev_time), 0, 0, true); // print prev time on LCD
      delay(min_run_length);
      
      while(digitalRead(photo_pin)!=input_start){
        result_time = millis()-start_time;
        print_ln_lcd(ms_to_print(result_time), 0, 1); // update time on LCD
      }
      
      run_on = false;
      prev_time = result_time; // save the result time as the previous time for LCD display
      Serial.println(result_time);
      delay(min_run_length);
    }
  }

}

// functions definitions
void print_ln_lcd(String message, int col=0, int row=0, bool clear=false){ // print message to LCD
  if(clear){
    lcd.clear();
  }
  lcd.setCursor(col, row);
  lcd.print(message);
}

String ms_to_print(long int ms){ // convert milliseconds to string
  String result = "";
  int sec = ms/1000;
  int min = sec/60;
  int hr = min/60;
  if(hr>0){
    result += String(hr)+":";
  }
  if(min>0){
    if(min%60<10){
      result += "0";
    }
    result += String(min%60)+":";
  }
  if(sec>0){
    if(sec%60<10){
      result += "0";
    }
    result += String(sec%60)+".";
  }
  if(ms>0){
    result += String(ms%1000);
  }
  return result;
}
