# Fritzing sketch start (saved by Fritzing 0.9.10b)
breadboards: 1

parts:
  Arduino_Uno_R3 = Arduino Uno (Rev3) - ICSP
  HC-12 = HC-12 Module
  S1 = SWITCH-MOMENTARY-2 [package=reed_switch_pth]
  Battery_9v = BC9VPC [package=bc9vpc]

nets:
  5V: Arduino_Uno_R3.5V, HC-12.VCC
  GND: Arduino_Uno_R3.GND, HC-12.GND, S1.1, Battery_9v.V-
  N1: Arduino_Uno_R3.D8, HC-12.RXD
  N2: Arduino_Uno_R3.D9_PWM, HC-12.TXD
  N3: Arduino_Uno_R3.D7, S1.2
  N4: Arduino_Uno_R3.VIN, Battery_9v.V+

custom parts:
  HC-12 Module: HC-12 433Mhz Module
